// Logisim project seq_circuit.circ as structural Verilog: 1 circuit, main circuit main
module main (
  input  X,
  input  Y,
  output S
);

  wire and_1_out, and_2_out, Clock_out, D_Flip_Flop_q, or_1_out, xor_1_out;

  xor xor_1 (xor_1_out, X, Y);
  and and_1 (and_1_out, X, Y);
  Clock Clock (.out(Clock_out));
  xor xor_2 (S, xor_1_out, D_Flip_Flop_q);
  and and_2 (and_2_out, xor_1_out, D_Flip_Flop_q, D_Flip_Flop_q);
  D_Flip_Flop D_Flip_Flop (.clk(Clock_out), .D(or_1_out), .Q(D_Flip_Flop_q));  // open: Qn, preset, en, reset
  or or_1 (or_1_out, and_2_out, and_1_out);

  // Notes on the sheet:
  //   Q
  //   Q
  //   C
endmodule
